# Fritzing sketch schematic (saved by Fritzing 0.9.3b)
breadboards: 1

parts:
  Flex_sensor_-_index = Basic Flex Resistor
  Slide_potentiometer = Slide Potentiometer [maximum_resistance=10kΩ]
  Battery = LIPO-2000mAh [package=lipo-2000]
  Battery_charge_circuit = Power Cell LiPo Charger/Booster
  Power_switch = Header 2 [package=r_sw_th]
  uC = Arduino Nano (Rev3.0) (ICSP)
  Flex_sensor_-_thumb = Basic Flex Resistor
  Flex_sensor_-_pinky = Basic Flex Resistor
  R1 = Resistor [tolerance=±5% resistance=47k package="0603 [SMD]"]
  R2 = Resistor [tolerance=±5% resistance=47k package="0603 [SMD]"]
  R5 = Resistor [tolerance=±5% resistance=47k package="0603 [SMD]"]
  USB_charging_connector = USB Connectors [package=usb-minib]
  Force_sensor_-_thumb = Basic Force Sensing Resistor (FSR) [package=THT]
  Force_sensor_-_index = Basic Force Sensing Resistor (FSR) [package=THT]
  R7 = Resistor [tolerance=±5% resistance=3.3k package="0603 [SMD]"]
  R6 = Resistor [tolerance=±5% resistance=3.3k package="0603 [SMD]"]
  J1 = Basic Servo
  Q2 = PNP-Transistor [package="TO92 [THT]"]
  R8 = Resistor [tolerance=±5% resistance=1k package="2512 [SMD]"]
  Rotary_encoder = Rotary Encoder [package=THT]
  R9 = Resistor [tolerance=±5% resistance=10k package="2010 [SMD]"]
  R10 = Resistor [tolerance=±5% resistance=10k package="2010 [SMD]"]

nets:
  N1: Flex_sensor_-_index.Pin_2, Slide_potentiometer.leg2, uC.5V, Flex_sensor_-_thumb.Pin_2, Flex_sensor_-_pinky.Pin_2, Force_sensor_-_thumb.pin_0, Force_sensor_-_index.pin_0, Rotary_encoder.EncoderPinC
  N2: Flex_sensor_-_index.pin_1, uC.A2, R2.Pin_1
  GND: Slide_potentiometer.leg1, Battery.-, Battery_charge_circuit.GND, Power_switch.2, uC.GND, R1.Pin_0, R2.Pin_0, R5.Pin_0, USB_charging_connector.GND, R7.Pin_0, R6.Pin_0, J1.gnd, R9.Pin_1, R10.Pin_1
  N3: Slide_potentiometer.wiper, uC.A0
  N4: Battery.+, Battery_charge_circuit.VBATT
  VCC: Battery_charge_circuit.VCC, uC.VIN, Q2.E
  N5: Battery_charge_circuit.5VIN, USB_charging_connector.D+
  N6: Battery_charge_circuit.EN, Power_switch.1
  N7: uC.D2, Rotary_encoder.EncoderPinB, R10.Pin_0
  N8: uC.D3, Rotary_encoder.EncoderPinA, R9.Pin_0
  N9: uC.D9, J1.pulse
  N10: uC.D10, R8.Pin_0
  N11: uC.A6, Force_sensor_-_index.pin_1, R7.Pin_1
  N12: uC.A5, Force_sensor_-_thumb.pin_1, R6.Pin_1
  N13: uC.A4, Flex_sensor_-_pinky.pin_1, R5.Pin_1
  N14: uC.A1, Flex_sensor_-_thumb.pin_1, R1.Pin_1
  N15: J1.vcc, Q2.C
  N16: Q2.B, R8.Pin_1
